// Digital circuit dl8.dig as structural Verilog
module dl8 (
  input  EN,
  input  [7:0] D,
  output [7:0] Q
);

  wire relaydt_1_p1, relaydt_1_p4, relaydt_2_p6, relaydt_5_p1, relaydt_5_p4, relaydt_6_p6, relaydt_9_p1,
       relaydt_9_p4, relaydt_10_p6, relaydt_13_p1, relaydt_13_p4, relaydt_14_p6, relaydt_17_p1,
       relaydt_17_p4, relaydt_18_p6, relaydt_21_p1, relaydt_21_p4, relaydt_22_p6, relaydt_25_p1,
       relaydt_25_p4, relaydt_26_p6, relaydt_29_p1, relaydt_29_p4, relaydt_30_p6;

  PullDown #(.Bits(8)) pulldown_1 (.out(Q));
  // RelayDT relaydt_1: pin names not known; wires that end beside it: relaydt_1_p1, D[7], 1'b0, relaydt_1_p4
  // RelayDT relaydt_2: pin names not known; wires that end beside it: EN, 1'b1, relaydt_1_p4, 1'b0, relaydt_1_p1, relaydt_2_p6, 1'b0
  // RelayDT relaydt_3: pin names not known; wires that end beside it: relaydt_1_p4, relaydt_2_p6, 1'b0
  // RelayDT relaydt_4: pin names not known; wires that end beside it: 1'b1, Q[7]
  // RelayDT relaydt_5: pin names not known; wires that end beside it: relaydt_5_p1, D[6], 1'b0, relaydt_5_p4
  // RelayDT relaydt_6: pin names not known; wires that end beside it: EN, 1'b1, relaydt_5_p4, 1'b0, relaydt_5_p1, relaydt_6_p6, 1'b0
  // RelayDT relaydt_7: pin names not known; wires that end beside it: relaydt_5_p4, relaydt_6_p6, 1'b0
  // RelayDT relaydt_8: pin names not known; wires that end beside it: 1'b1, Q[6]
  // RelayDT relaydt_9: pin names not known; wires that end beside it: relaydt_9_p1, D[5], 1'b0, relaydt_9_p4
  // RelayDT relaydt_10: pin names not known; wires that end beside it: EN, 1'b1, relaydt_9_p4, 1'b0, relaydt_9_p1, relaydt_10_p6, 1'b0
  // RelayDT relaydt_11: pin names not known; wires that end beside it: relaydt_9_p4, relaydt_10_p6, 1'b0
  // RelayDT relaydt_12: pin names not known; wires that end beside it: 1'b1, Q[5]
  // RelayDT relaydt_13: pin names not known; wires that end beside it: relaydt_13_p1, D[4], 1'b0, relaydt_13_p4
  // RelayDT relaydt_14: pin names not known; wires that end beside it: EN, 1'b1, relaydt_13_p4, 1'b0, relaydt_13_p1, relaydt_14_p6, 1'b0
  // RelayDT relaydt_15: pin names not known; wires that end beside it: relaydt_13_p4, relaydt_14_p6, 1'b0
  // RelayDT relaydt_16: pin names not known; wires that end beside it: 1'b1, Q[4]
  // RelayDT relaydt_17: pin names not known; wires that end beside it: relaydt_17_p1, D[3], 1'b0, relaydt_17_p4
  // RelayDT relaydt_18: pin names not known; wires that end beside it: EN, 1'b1, relaydt_17_p4, 1'b0, relaydt_17_p1, relaydt_18_p6, 1'b0
  // RelayDT relaydt_19: pin names not known; wires that end beside it: relaydt_17_p4, relaydt_18_p6, 1'b0
  // RelayDT relaydt_20: pin names not known; wires that end beside it: 1'b1, Q[3]
  // RelayDT relaydt_21: pin names not known; wires that end beside it: relaydt_21_p1, D[2], 1'b0, relaydt_21_p4
  // RelayDT relaydt_22: pin names not known; wires that end beside it: EN, 1'b1, relaydt_21_p4, 1'b0, relaydt_21_p1, relaydt_22_p6, 1'b0
  // RelayDT relaydt_23: pin names not known; wires that end beside it: relaydt_21_p4, relaydt_22_p6, 1'b0
  // RelayDT relaydt_24: pin names not known; wires that end beside it: 1'b1, Q[2]
  // RelayDT relaydt_25: pin names not known; wires that end beside it: relaydt_25_p1, D[1], 1'b0, relaydt_25_p4
  // RelayDT relaydt_26: pin names not known; wires that end beside it: EN, 1'b1, relaydt_25_p4, 1'b0, relaydt_25_p1, relaydt_26_p6, 1'b0, relaydt_25_p1
  // RelayDT relaydt_27: pin names not known; wires that end beside it: relaydt_25_p4, relaydt_26_p6, 1'b0
  // RelayDT relaydt_28: pin names not known; wires that end beside it: 1'b1, Q[1]
  // RelayDT relaydt_29: pin names not known; wires that end beside it: relaydt_29_p1, D[0], 1'b0, relaydt_29_p4
  // RelayDT relaydt_30: pin names not known; wires that end beside it: EN, 1'b1, relaydt_29_p4, 1'b0, relaydt_29_p1, relaydt_30_p6, 1'b0, EN, relaydt_29_p1
  // RelayDT relaydt_31: pin names not known; wires that end beside it: relaydt_29_p4, relaydt_30_p6, 1'b0
  // RelayDT relaydt_32: pin names not known; wires that end beside it: 1'b1, Q[0]
endmodule
