// Digital circuit top.dig as structural Verilog
module top (
  input  PHI1,
  input  PHI2,
  input  CK,
  input  AUTO
);

  wire A, ADDC, Ai, ALUOP, AMUXS, and_1_out, and_3_out, and_9_out, and_10_out, and_12_out, and_13_out, B,
       BRTAKEN, button_1_out, button_2_out, button_3_out, button_4_out, C1i, C1o, C2o, comparator_1_eq,
       demultiplexer_2_out_0, demultiplexer_2_out_2, Di, DLEN, LONG, multiplexer_8_out, not_1_out, not_2_out,
       PHI1_t, PHI2_t, RAMWE, relaydt_1_p1, relaydt_1_p4, relaydt_2_p6, relaydt_5_p4, relaydt_6_p1,
       relaydt_6_p4, relaydt_7_p6, relaydt_10_p1, relaydt_10_p4, relaydt_11_p6, relaydt_14_p1, relaydt_14_p4,
       relaydt_15_p1, relaydt_15_p4, relaydt_16_p6, relaydt_19_p6, relaydt_22_p1, relaydt_22_p4,
       relaydt_23_p1, relaydt_23_p6, RETOP, STOREOP, xnor_1_out, xnor_2_out, xor_2_out, xor_3_out, ZF;
  wire [1:0] and_7_out, counter_1_out;
  wire [2:0] ALUC;
  wire [7:0] A1, A2, add_1_s, AMUX, and_11_out, BMUX, DL, multiplexer_1_out, multiplexer_4_out, neg_1_out,
       or_3_out, ramasync_1_q, RAMD, xor_1_out;
  wire [11:0] add_2_s, multiplexer_5_out, multiplexer_7_out, PC1, PC2;
  wire [15:0] IL, PROGRAM_d, ROMD;

  // Probe on PC2
  ROM #(.AddrBits(12), .Bits(16)) PROGRAM (.A(PC2), .sel(1'b1), .D(PROGRAM_d));
  Delay #(.Bits(16), .delayTime(3)) delay_1 (.in(PROGRAM_d), .out(ROMD));
  // Probe on ROMD
  and and_1 (and_1_out, Ai, PHI1_t);
  Multiplexer #(.Bits(8)) multiplexer_1 (.sel(B), .in_0(ROMD[7:0]), .in_1(RAMD), .out(multiplexer_1_out));
  dl8 dl8_1 (.EN(and_1_out), .D(ROMD[15:8]), .Q({IL[15:13], ALUC, IL[9:8]}));
  dl8 dl8_2 (.EN(PHI1_t), .D(multiplexer_1_out), .Q(IL[7:0]));
  // Probe on {IL[15:13], ALUC, IL[9:0]}
  and and_2 (AMUXS, IL[9], not_1_out);
  not not_1 (not_1_out, A);
  Button button_1 (.out(button_1_out));
  Button button_2 (.out(button_2_out));
  Button button_3 (.out(button_3_out));
  not not_2 (not_2_out, IL[15]);
  Button button_4 (.out(button_4_out));
  Comparator #(.Bits(12)) comparator_1 (.a(PC2), .b(12'hffe), .eq(comparator_1_eq));  // open: gt, lt
  and and_3 (and_3_out, Di, PHI2_t);
  Stop stop_1 (.stop(comparator_1_eq));
  and and_4 (LONG, IL[9], not_2_out);
  Demultiplexer #(.Selector_Bits(2)) demultiplexer_1 (
    .sel(IL[14:13]), .in(not_2_out), .out_0(ALUOP), .out_1(STOREOP), .out_2(RETOP));  // open: out_3
  Multiplexer #(.Bits(8)) multiplexer_2 (.sel(AMUXS), .in_0(IL[7:0]), .in_1(DL), .out(AMUX));
  and and_5 (RAMWE, and_3_out, STOREOP);
  Counter #(.Bits(2)) counter_1 (.en(1'b1), .C(CK), .clr(1'b0), .out(counter_1_out));  // open: ovf
  Demultiplexer #(.Selector_Bits(2)) demultiplexer_2 (
    .sel(counter_1_out), .in(AUTO), .out_0(demultiplexer_2_out_0), .out_2(demultiplexer_2_out_2));  // open: out_1, out_3
  // Probe on AMUX
  RAMAsync #(.AddrBits(8), .Bits(8)) ramasync_1 (.A(AMUX), .D(A2), .we(RAMWE), .Q(ramasync_1_q));
  // RelayDT relaydt_1: pin names not known; wires that end beside it: relaydt_1_p1, Ai, 1'b0, relaydt_1_p4
  and and_6 (DLEN, Ai, PHI1_t);
  Delay #(.Bits(8), .delayTime(5)) delay_2 (.in(ramasync_1_q), .out(RAMD));
  // RelayDT relaydt_2: pin names not known; wires that end beside it: PHI1_t, 1'b1, relaydt_1_p4, 1'b0, relaydt_1_p1, relaydt_2_p6, 1'b0
  // RelayDT relaydt_3: pin names not known; wires that end beside it: relaydt_1_p4, relaydt_2_p6, 1'b0
  // RelayDT relaydt_4: pin names not known; wires that end beside it: 1'b1, A
  dl8 dl8_3 (.EN(DLEN), .D(RAMD), .Q(DL));
  // Probe on RAMD
  or or_1 (PHI1_t, PHI1, demultiplexer_2_out_0);
  PullDown pulldown_1 (.out(A));
  // RelayDT relaydt_5: pin names not known; wires that end beside it: A, LONG, Di, relaydt_5_p4, 1'b0
  or or_2 (PHI2_t, demultiplexer_2_out_2, PHI2);
  // RelayDT relaydt_6: pin names not known; wires that end beside it: relaydt_6_p1, relaydt_5_p4, 1'b0, relaydt_6_p4
  PullDown pulldown_2 (.out(relaydt_5_p4));
  // RelayDT relaydt_7: pin names not known; wires that end beside it: PHI2_t, 1'b1, relaydt_6_p4, 1'b0, relaydt_6_p1, relaydt_7_p6, 1'b0
  // RelayDT relaydt_8: pin names not known; wires that end beside it: relaydt_6_p4, relaydt_7_p6, 1'b0
  // RelayDT relaydt_9: pin names not known; wires that end beside it: 1'b1, B, Ai
  PullDown pulldown_3 (.out(B));
  // RelayDT relaydt_10: pin names not known; wires that end beside it: relaydt_10_p1, B, 1'b0, relaydt_10_p4
  // Probe on BRTAKEN
  // Probe on PC1
  // Probe on PC2
  // Probe on ROMD
  // Probe on {IL[15:13], ALUC, IL[9:0]}
  // RelayDT relaydt_11: pin names not known; wires that end beside it: PHI1_t, 1'b1, relaydt_10_p4, 1'b0, relaydt_10_p1, relaydt_11_p6, 1'b0
  // RelayDT relaydt_12: pin names not known; wires that end beside it: relaydt_10_p4, relaydt_11_p6, 1'b0
  // RelayDT relaydt_13: pin names not known; wires that end beside it: 1'b1, Di
  and and_7 (and_7_out[0], ALUC[1], ALUC[2]);
  and and_8 (and_7_out[1], ALUC[0], ALUC[1]);
  PullDown pulldown_4 (.out(Di));
  Multiplexer #(.Selector_Bits(2)) multiplexer_3 (
    .sel(and_7_out), .in_0(ADDC), .in_1(A2[7]), .in_2(A2[0]), .in_3(C2o), .out(C1i));
  // RelayDT relaydt_14: pin names not known; wires that end beside it: relaydt_14_p1, C1i, 1'b0, relaydt_14_p4
  // RelayDT relaydt_15: pin names not known; wires that end beside it: relaydt_15_p1, Di, 1'b0, relaydt_15_p4
  dl8 dl8_4 (.EN(PHI1_t), .D(multiplexer_4_out), .Q(A1));
  // RelayDT relaydt_16: pin names not known; wires that end beside it: PHI1_t, 1'b1, relaydt_14_p4, 1'b0, relaydt_14_p1, relaydt_16_p6, 1'b0
  // RelayDT relaydt_17: pin names not known; wires that end beside it: relaydt_14_p4, relaydt_16_p6, 1'b0
  // RelayDT relaydt_18: pin names not known; wires that end beside it: 1'b1, C1o
  // Probe on RAMWE
  // Probe on DL
  // Probe on RAMD
  // Probe on AMUX
  // Probe on AMUXS
  // RelayDT relaydt_19: pin names not known; wires that end beside it: PHI2_t, 1'b1, relaydt_15_p4, 1'b0, relaydt_15_p1, relaydt_19_p6, 1'b0
  // RelayDT relaydt_20: pin names not known; wires that end beside it: relaydt_15_p4, relaydt_19_p6, 1'b0
  // RelayDT relaydt_21: pin names not known; wires that end beside it: 1'b1, Ai
  Add #(.Bits(8)) add_1 (.a(A2), .b(BMUX), .c_i(C2o), .s(add_1_s), .c_o(ADDC));
  PullDown pulldown_5 (.out(Ai));
  and and_9 (and_9_out, Di, ALUOP);
  and and_10 (and_10_out, and_9_out, PHI2_t);
  Multiplexer #(.Selector_Bits(3), .Bits(8)) multiplexer_4 (
    .sel(ALUC), .in_0(BMUX), .in_1(neg_1_out), .in_2(or_3_out), .in_3(xor_1_out), .in_4(and_11_out),
    .in_5(add_1_s), .in_6({C2o, A2[7:1]}), .in_7({A2[6:0], C2o}), .out(multiplexer_4_out));
  // Probe on A1
  // Probe on A2
  // Probe on BMUX
  Neg #(.Bits(8)) neg_1 (.in(BMUX), .out(neg_1_out));
  dl8 dl8_5 (.EN(and_10_out), .D(A1), .Q(A2));
  assign and_11_out = BMUX & A2;  // And and_11, 8 bits wide
  assign xor_1_out = BMUX ^ A2;  // XOr xor_1, 8 bits wide
  // RelayDT relaydt_22: pin names not known; wires that end beside it: relaydt_22_p1, C1o, 1'b0, relaydt_22_p4
  and and_12 (and_12_out, Di, PHI2_t);
  Comparator #(.Bits(8)) comparator_2 (.a(A2), .b({8{1'b0}}), .eq(ZF));  // open: gt, lt
  assign or_3_out = BMUX | A2;  // Or or_3, 8 bits wide
  // RelayDT relaydt_23: pin names not known; wires that end beside it: relaydt_23_p1, 1'b1, relaydt_22_p4, 1'b0, relaydt_22_p1, relaydt_23_p6, 1'b0
  // RelayDT relaydt_24: pin names not known; wires that end beside it: relaydt_22_p4, relaydt_23_p6, 1'b0
  // RelayDT relaydt_25: pin names not known; wires that end beside it: 1'b1, C2o
  dl8 dl8_6 (.EN(and_12_out), .D(PC1[7:0]), .Q(PC2[7:0]));
  dl4 dl4_1 (.EN(and_12_out), .D(PC1[11:8]), .Q(PC2[11:8]));
  Multiplexer #(.Bits(12)) multiplexer_5 (
    .sel(1'b0), .in_0({ALUC[1:0], IL[9:0]}), .in_1({DL[7:4], IL[7:0]}), .out(multiplexer_5_out));
  and and_13 (and_13_out, Di, ALUOP);
  // Probe on PC2
  Add #(.Bits(12)) add_2 (.a(PC2), .b(12'h1), .c_i(1'b0), .s(add_2_s));  // open: c_o
  // Probe on DL
  // Probe on IL[7:0]
  Multiplexer #(.Bits(8)) multiplexer_6 (.sel(IL[8]), .in_0(IL[7:0]), .in_1(DL), .out(BMUX));
  and and_14 (relaydt_23_p1, and_13_out, PHI2_t);
  Multiplexer #(.Bits(12)) multiplexer_7 (
    .sel(BRTAKEN), .in_0(add_2_s), .in_1(multiplexer_5_out), .out(multiplexer_7_out));
  xnor xnor_1 (xnor_1_out, C2o, IL[13]);
  xnor xnor_2 (xnor_2_out, IL[14], ZF);
  xor xor_2 (xor_2_out, ALUC[2], xnor_1_out);
  xor xor_3 (xor_3_out, ALUC[2], xnor_2_out);
  Multiplexer #(.Selector_Bits(2)) multiplexer_8 (
    .sel({IL[13], IL[14]}), .in_0(1'b0), .in_1(xor_3_out), .in_2(xor_2_out), .in_3(IL[15]),
    .out(multiplexer_8_out));
  and and_15 (BRTAKEN, IL[15], multiplexer_8_out);
  dl8 dl8_7 (.EN(PHI1_t), .D(multiplexer_7_out[7:0]), .Q(PC1[7:0]));
  dl4 dl4_2 (.EN(PHI1_t), .D(multiplexer_7_out[11:8]), .Q(PC1[11:8]));
  // Probe on PC1

  // Other names for the same wires on the sheet: ROR = A2[0]; ROL = A2[7]; C2i = C1o; CF = C2o;
  //   ILhi[7:0] = {IL[15:13], ALUC, IL[9:8]}; SELB = IL[8]; IND = IL[9]; IL[12:10] = ALUC; ILlo[7:0] = IL[7:0]

  // Notes on the sheet:
  //   CK: Hz: 120
  //   contents of PROGRAM (hex, n*v repeats v):
  //   ffff,fa,2003,11,103,4,2005,42,2205,ff,205,2006,4083*0,f001
  //   IL and mux R:36
  //   IL[8] controls BMUX
  //   0 - ILlow immediate
  //   1 - DLATCH absolute
  //   PHI1 PHI2 R:2
  //   input conversion
  //   SEQUENCER 4 BITS 2H 2EN R:8
  //   (NO LOGIC AROUND)
  //   A1 R:16
  //   Carry flag
  //   A2 R:16
  //   RETMUX 4bit R:2
  //   PC2 R:24
  //   INCR XOR R:3
  //   BRMUX R:6
  //   BR LOGIC R:5
  //   2 for mux,
  //   1 shared xor
  //   2 xors for C Z
  //   PC1 R:24
endmodule
